# Fritzing sketch ov7670 (saved by Fritzing 0.9.2b)
breadboards: 1

parts:
  パーツ1 = Arduino Uno (Rev3)
  IC1 = IC, DIP package, 18 pins [chip_label=ov7670]
  R1 = Resistor [tolerance=±5% resistance=10k package=THT]
  R2 = Resistor [tolerance=±5% resistance=10k package=THT]
  R3 = Resistor [tolerance=±5% resistance=4.7k package=THT]
  R4 = Resistor [tolerance=±5% resistance=4.7k package=THT]

nets:
  N1: パーツ1.A0, IC1.pin11
  N2: パーツ1.A1, IC1.pin8
  N3: パーツ1.A2, IC1.pin12
  N4: パーツ1.A3, IC1.pin7
  N5: パーツ1.A4/SDA, IC1.pin17, R2.Pin_1
  N6: パーツ1.A5/SCL, IC1.pin2, R1.Pin_1
  N7: パーツ1.D8, IC1.pin16
  N8: パーツ1.D11_PWM/MOSI, R3.Pin_1
  N9: パーツ1.GND, IC1.pin10, IC1.pin18, R4.Pin_0
  N10: パーツ1.D2, IC1.pin4
  N11: パーツ1.D3_PWM, IC1.pin3
  N12: パーツ1.D4, IC1.pin13
  N13: パーツ1.D5_PWM, IC1.pin6
  N14: パーツ1.D6_PWM, IC1.pin14
  N15: パーツ1.D7, IC1.pin5
  N16: パーツ1.3V3, IC1.pin1, IC1.pin9, R1.Pin_0, R2.Pin_0
  N17: IC1.pin15, R3.Pin_0, R4.Pin_1
